// Logisim project Lab3.circ as structural Verilog
module full_adder (
  input  A,
  input  Cin,
  input  B,
  output S,
  output Cout
);

  wire and_1_out, and_2_out, xor_1_out;

  and and_1 (and_1_out, A, B);
  xor xor_1 (xor_1_out, A, B);
  xor xor_2 (S, xor_1_out, Cin);
  and and_2 (and_2_out, Cin, xor_1_out);
  or or_1 (Cout, and_2_out, and_1_out);
endmodule

module ripple_carry4 (
  input  [3:0] in_1,
  input  Cin,
  input  [3:0] in_3,
  output [3:0] out_4,
  output Cout
);

  wire full_adder_1_cout, full_adder_2_cout, full_adder_3_cout;

  full_adder full_adder_1 (.A(in_1[0]), .Cin(Cin), .B(in_3[0]), .S(out_4[0]), .Cout(full_adder_1_cout));
  full_adder full_adder_2 (.A(in_1[1]), .Cin(full_adder_1_cout), .B(in_3[1]), .S(out_4[1]), .Cout(full_adder_2_cout));
  full_adder full_adder_3 (.A(in_1[2]), .Cin(full_adder_2_cout), .B(in_3[2]), .S(out_4[2]), .Cout(full_adder_3_cout));
  full_adder full_adder_4 (.A(in_1[3]), .Cin(full_adder_3_cout), .B(in_3[3]), .S(out_4[3]), .Cout(Cout));
endmodule

module op0 (
  input  [3:0] A,
  output [7:0] ALUout
);

  wire [3:0] ripple_carry4_1_out_4;
  wire [4:4] ripple_carry4_1_cout;

  ripple_carry4 ripple_carry4_1 (
    .in_1(A), .Cin(1'b0), .in_3(4'b0001), .out_4(ripple_carry4_1_out_4), .Cout(ripple_carry4_1_cout[4]));
  assign ALUout = {{3{1'b0}}, {ripple_carry4_1_cout[4], ripple_carry4_1_out_4}};  // Bit_Extender bit_extender_1
endmodule

module op2 (
  input  [3:0] A,
  input  [3:0] B,
  output [7:0] ALUout
);

  wire [7:0] bit_extender_1_out, bit_extender_2_out;

  assign bit_extender_1_out = {{4{1'b0}}, A};  // Bit_Extender bit_extender_1
  assign bit_extender_2_out = {{4{B[3]}}, B};  // Bit_Extender bit_extender_2
  Adder adder_1 (.a(bit_extender_1_out), .b(bit_extender_2_out), .out(ALUout));  // open: cin, cout
endmodule

module op1 (
  input  [3:0] A,
  input  [3:0] B,
  output [7:0] ALUout
);

  wire [3:0] ripple_carry4_1_out_4;
  wire [4:4] ripple_carry4_1_cout;

  ripple_carry4 ripple_carry4_1 (
    .in_1(A), .Cin(1'b0), .in_3(B), .out_4(ripple_carry4_1_out_4), .Cout(ripple_carry4_1_cout[4]));
  assign ALUout = {{3{1'b0}}, {ripple_carry4_1_cout[4], ripple_carry4_1_out_4}};  // Bit_Extender bit_extender_1
endmodule
